# Fritzing sketch MODR_ard_01 (saved by Fritzing 0.9.3b)

parts:
  Part1 = Arduino Uno (Rev3)
  U1 = LIPO-2000mAh [package=lipo-2000]
  Part2 = PowerBoost 500 Charger
  Part4 = Motor Driver 1A Dual TB6612FNG
  U2 = SWITCH_SPDT [package=kps-1290]
  LEFT_(B) = DC Motor with two-phase hall-encoder
  RIGHT_(A) = DC Motor with two-phase hall-encoder [part_number=VT-E-G25A-06-177E]

nets:
  N1: Part1.D10_PWM/SS, Part4.PWMA
  N2: Part1.D11_PWM/MOSI, Part4.PWMB
  N3: Part1.D12/MISO, Part4.STBY
  N4: Part1.D2, LEFT_(B).pin4
  N5: Part1.D3_PWM, RIGHT_(A).pin4
  N6: Part1.D4, LEFT_(B).pin5
  N7: Part1.D5_PWM, RIGHT_(A).pin5
  5V: Part1.5V, Part2.5.0V, Part4.VCC, LEFT_(B).pin3, RIGHT_(A).pin3
  GND: Part1.GND, U1.-, Part2.GND, Part4.GND, LEFT_(B).pin6, RIGHT_(A).pin6
  N8: U1.+, U2.P
  N9: Part2.VBAT, U2.S
  N10: Part4.B01, LEFT_(B).pin1
  N11: Part4.B02, LEFT_(B).pin2
  N12: Part4.A02, RIGHT_(A).pin2
  N13: Part4.A01, RIGHT_(A).pin1

custom parts:
  PowerBoost 500 Charger: The PowerBoost 500C is a little DC/DC boost converter module that can be powered by any 3.7V LiIon/LiPoly battery, and convert the battery output to 5.2V DC for running your 5V projects. At its heart is a TPS61090 boost converter from TI. This boost converter chip has some really nice extras such as low battery detection, 2A internal switch, synchronous conversion, excellent efficiency, and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
